# Fritzing sketch Project (saved by Fritzing 0.9.9b)

parts:
  A1 = GY-BMP280 Breakout
  A2 = DHT22 module
  microSD1 = MicroSD Card Module
  U2 = ESP8266-01S [part_number=ESP8266]
  M1 = DC Motor
  M2 = DC Motor
  M3 = DC Motor
  M4 = DC Motor
  L298N1 = L298N DC motor driver
  L298N2 = L298N DC motor driver
  S1 = Toggle Switch [package=THT]
  BAT1 = Battery
  Часть3 = Arduino Mega 2560 (Rev3)
  HC-SR04_Sensor_1 = HC-SR04 Ultrasonic Distance Sensor

nets:
  VCC: A1.Pin_1, A2.+, microSD1.VCC, Часть3.5V, HC-SR04_Sensor_1.VCC
  GND: A1.Pin_2, A2.-, microSD1.GND, U2.GND, Часть3.GND, HC-SR04_Sensor_1.GND
  N1: A1.Pin_3, Часть3.D21/SCL
  N2: A1.Pin_4, Часть3.D20/SDA
  N3: A2.Out, Часть3.D31
  N4: microSD1.MISO, Часть3.D23
  N5: microSD1.MOSI, Часть3.D25
  N6: microSD1.SCK, Часть3.D27
  N7: microSD1.CS, Часть3.D29
  N8: U2.RXD, U2.GPIO_0, Часть3.D17_PWM/RX2
  VCC_2: U2.VCC, U2.RST, U2.CH_PD, Часть3.3V3
  N9: U2.TXD, Часть3.D16_PWM/TX2
  N10: M1.pin_1, L298N2.OUT4
  N11: M1.pin_2, L298N2.OUT3
  N12: M2.pin_1, L298N2.OUT2
  N13: M2.pin_2, L298N2.OUT1
  N14: M3.pin_1, L298N1.OUT2
  N15: M3.pin_2, L298N1.OUT1
  N16: M4.pin_1, L298N1.OUT4
  N17: M4.pin_2, L298N1.OUT3
  N18: L298N1.ENA, L298N1.ENB, L298N2.ENA, Часть3.D6_PWM
  N19: L298N1.IN1, Часть3.D2_PWM
  N20: L298N1.IN2, Часть3.D3_PWM
  N21: L298N1.IN3, Часть3.D4_PWM
  N22: L298N1.IN4, Часть3.D5_PWM
  N23: L298N2.GND, BAT1.-
  N24: L298N2.IN1, Часть3.D8_PWM
  N25: L298N2.IN2, Часть3.D9_PWM
  N26: L298N2.IN3, Часть3.D10_PWM
  N27: L298N2.IN4, Часть3.D11_PWM
  N28: S1.COM, BAT1.+
  N29: Часть3.D33, HC-SR04_Sensor_1.TRIG
  N30: Часть3.D35, HC-SR04_Sensor_1.ECHO

custom parts:
  DHT22 module: DHT22 module. Pins VCC Data GND.
  MicroSD Card Module: A common microSD card module.
  L298N DC motor driver: 2x DC motor driver with 78M05 positive voltage regulator (7..35 V) L298N: max 46 V, 2 A Set 5 V Enable jumper to enable 5 V regultor (needed for the L298N) and +5 V output at screw terminal or supply external +5 V at screw terminal Set ENA and/or ENB to +5 V to enable motor permanently or supply ENA and/or ENB with PWM signal IN1 and IN2 set rotation directory for motor A (OUT1/OUT2) IN2 and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
  Battery: Your standard 2x 18650 battery pack (7.4 Volts)
